# Fritzing sketch Sketch (saved by Fritzing 0.9.3b)
breadboards: 1

parts:
  U1 = NodeMCU V1.0
  R1 = Resistor [tolerance=±5% resistance=330 package="0603 [SMD]"]
  R2 = Resistor [tolerance=±5% resistance=330 package="0603 [SMD]"]
  R3 = Resistor [tolerance=±5% resistance=330 package="0603 [SMD]"]
  R4 = Resistor [tolerance=±5% resistance=330 package="0603 [SMD]"]
  R5 = Resistor [tolerance=±5% resistance=330 package="0603 [SMD]"]
  R6 = Resistor [tolerance=±5% resistance=330 package="0603 [SMD]"]
  LED1 = smd LED [color="Red (633nm)" package="0603 [SMD]"]
  LED2 = smd LED [color="Red (633nm)" package="0603 [SMD]"]
  LED3 = smd LED [color="Red (633nm)" package="0603 [SMD]"]
  LED4 = smd LED [color="Red (633nm)" package="0603 [SMD]"]
  LED5 = smd LED [color="Red (633nm)" package="0603 [SMD]"]
  LED6 = smd LED [color="Red (633nm)" package="0603 [SMD]"]

nets:
  N1: U1.GND, LED1.cathode, LED2.cathode, LED3.cathode, LED4.cathode, LED5.cathode, LED6.cathode
  N2: U1.D5, R6.Pin_0
  N3: U1.D6, R5.Pin_0
  N4: U1.D7, R4.Pin_0
  N5: U1.D8, R3.Pin_0
  N6: U1.RX, R2.Pin_0
  N7: U1.TX, R1.Pin_0
  N8: R1.Pin_1, LED6.anode
  N9: R2.Pin_1, LED4.anode
  N10: R3.Pin_1, LED3.anode
  N11: R4.Pin_1, LED1.anode
  N12: R5.Pin_1, LED2.anode
  N13: R6.Pin_1, LED5.anode

custom parts:
  NodeMCU V1.0: ESP8266 based NodeMCU
